# Fritzing sketch line_trace_lap_timer (saved by Fritzing 0.9.5d)
circuit board: 8.46667cm x 5.64444cm
breadboards: 1

parts:
  A1 = MH-FMD buzzer
  A2 = Arduino R4 Minima
  M1 = fc-51 [package=THT]
  OLED1 = OLED 128x64 I2C Monochrome Display GND-VDD

nets:
  N1: A1.Pin_1, A2.Pin_5, M1.pin3, OLED1.VDD
  N2: A1.Pin_2, A2.Pin_39
  N3: A1.Pin_3, A2.Pin_6, A2.Pin_7, A2.Pin_45, M1.pin2, OLED1.GND
  N4: A2.Pin_13, OLED1.SDA
  N5: A2.Pin_14, OLED1.SCK
  N6: A2.Pin_33, M1.pin1

custom parts:
  MH-FMD buzzer: MH-FMD buzzer.
  Arduino R4 Minima: Introducing the Arduino UNO R4 Minima! This board boasts the RA4M1 microprocessor from Renesas, delivering increased processing power, expanded memory, and additional peripherals.
  OLED 128x64 I2C Monochrome Display GND-VDD: OLED 128x64 I2C Monochrome Display. Note: there are two variants of this part, this one is the GND VDD SCK SDA variant. The other is VDD GND SCK SDA. Make sure you select the part that matches your module as using the incorrect part will probably destroy your module! In addition the mounting holes are marked on silkscreen but not by default drilled. If you want drilled mounting holes, copy a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
